# Fritzing sketch FritzingCircuit (saved by Fritzing 0.9.4)
circuit board: 8.46667cm x 5.64444cm

parts:
  元件1 = Arduino Uno (Rev3)
  E1 = ESP32-Cam
  S1 = H-Bridge with L298N
  M1 = DC Motor
  M4 = DC Motor
  M3 = DC Motor
  M2 = DC Motor
  元件2 = Bluetooth HC-05 Macho
  BAT1 = Battery Holders [package=battery]

nets:
  N1: 元件1.D10_PWM/SS, 元件2.RXD
  N2: 元件1.D11_PWM/MOSI, 元件2.TXD
  GND: 元件1.GND, E1.GND, S1.GND, 元件2.GND, BAT1.-
  N3: 元件1.D4, S1.IN1
  N4: 元件1.D5_PWM, S1.IN2
  N5: 元件1.D6_PWM, S1.IN3
  N6: 元件1.D7, S1.IN4
  5V: 元件1.5V, E1.5V, 元件2.VCC
  VIN: 元件1.VIN, S1.5V, BAT1.+
  N7: S1.M1-01, M4.pin_2, M3.pin_2
  N8: S1.M1-02, S1.M2-01, S1.M2-02, S1.ENA-5V, S1.ENB-5V, M1.pin_1, M1.pin_2, M4.pin_1, M3.pin_1, M2.pin_1, M2.pin_2

custom parts:
  H-Bridge with L298N: h-bridge
